// Logisim project 2026-03-11-logic-circuit-1.circ as structural Verilog: 2 circuits, main circuit main
module main (
);

  wire and_1_out, and_2_out, and_3_out, and_4_out, and_5_out, and_6_out, and_7_out, and_8_out, and_9_out,
       and_10_out, and_11_out, and_12_out, and_13_out, button_1_out, clock_1_out, clock_2_out,
       CommandIndex_carry, d_ff_1_q, d_ff_2_qn, FrameDelayCounter_carry, j_k_ff_1_qn, j_k_ff_2_qn, not_1_out,
       not_2_out, not_3_out, not_4_out, not_5_out, not_6_out, not_7_out, not_8_out, not_9_out, not_10_out,
       not_11_out, not_12_out, or_1_out, or_2_out, or_3_out, or_4_out, or_5_out, or_6_out, or_7_out,
       por_1_out, sn76489_mockup_1_ready, TempoCounter_carry;
  wire [3:0] CommandIndex_q, rom_1_data;
  wire [7:0] ClockDivider_q, TempoRegister_q;
  wire [7:4] rom_1_data_2;
  wire [14:0] AddressCounter_q, LoopTarget_q;

  Clock clock_1 (.out(clock_1_out));
  POR #(.PorHighDuration(1)) por_1 (.out(por_1_out));
  or or_1 (or_1_out, por_1_out, button_1_out);
  Counter ClockDivider (.clr(or_1_out), .clk(clock_1_out), .Q(ClockDivider_q));  // open: load, up, count, D, carry
  Button button_1 (.out(button_1_out));
  Register TempoRegister (
    .D({rom_1_data_2, rom_1_data}), .en(1'b1), .clk(and_4_out), .Q(TempoRegister_q), .clr(or_1_out));
  Counter TempoCounter (
    .clr(or_1_out), .load(TempoCounter_carry), .up(1'b0), .clk(ClockDivider_q[6]),
    .D({1'b1, TempoRegister_q[6:0]}), .carry(TempoCounter_carry));  // open: count, Q
  and and_1 (and_1_out, TempoCounter_carry, FrameDelayCounter_carry);
  not not_1 (not_1_out, FrameDelayCounter_carry);
  not not_2 (not_2_out, or_2_out);
  or or_2 (or_2_out, TempoCounter_carry, and_5_out);
  D_Flip_Flop d_ff_1 (.D(and_1_out), .clk(ClockDivider_q[5]), .Q(d_ff_1_q), .reset(or_1_out));  // open: Qn, preset
  Counter FrameDelayCounter (
    .clr(or_1_out), .load(and_6_out), .up(1'b0), .count(not_1_out), .clk(not_2_out),
    .D({rom_1_data_2, rom_1_data}), .carry(FrameDelayCounter_carry));  // open: Q
  D_Flip_Flop d_ff_2 (.D(d_ff_1_q), .clk(not_3_out), .Qn(d_ff_2_qn), .reset(or_1_out));  // open: Q, preset
  not not_3 (not_3_out, ClockDivider_q[5]);
  and and_2 (and_2_out, d_ff_1_q, d_ff_2_qn);
  or or_3 (or_3_out, and_2_out, not_5_out);
  and and_3 (and_3_out, ClockDivider_q[5], or_3_out);
  or or_4 (or_4_out, and_8_out, and_3_out);
  Counter #(.max('h7fff), .width(15)) AddressCounter (
    .clr(or_1_out), .load(and_8_out), .clk(or_4_out), .D(LoopTarget_q), .Q(AddressCounter_q));  // open: up, count, carry
  and and_4 (and_4_out, not_4_out, and_10_out);
  ROM #(.addrWidth(15)) rom_1 (.addr(AddressCounter_q), .data({rom_1_data_2, rom_1_data}));
  // Probe on {rom_1_data_2, rom_1_data}
  and and_5 (and_5_out, not_4_out, and_6_out);
  // Probe on rom_1_data
  and and_6 (and_6_out, not_5_out, and_9_out);
  and and_7 (and_7_out, rom_1_data_2[7], not_4_out, CommandIndex_carry);
  not not_4 (not_4_out, and_3_out);
  not not_5 (not_5_out, CommandIndex_carry);
  Counter #(.max('hf), .width(4)) CommandIndex (
    .clr(or_1_out), .load(CommandIndex_carry), .up(1'b0), .clk(and_3_out), .D(rom_1_data),
    .carry(CommandIndex_carry), .Q(CommandIndex_q));  // open: count
  Register #(.width(15)) LoopTarget (
    .D(AddressCounter_q), .en(1'b1), .clk(and_7_out), .Q(LoopTarget_q), .clr(or_1_out));
  and and_8 (and_8_out, not_4_out, rom_1_data_2[6], CommandIndex_carry);
  not not_6 (not_6_out, CommandIndex_q[1]);
  not not_7 (not_7_out, CommandIndex_q[2]);
  not not_8 (not_8_out, CommandIndex_q[3]);
  and and_9 (and_9_out, not_8_out, not_7_out, not_6_out);
  and and_10 (and_10_out, CommandIndex_q[3], CommandIndex_q[2], CommandIndex_q[1]);
  or or_5 (or_5_out, and_9_out, and_10_out);
  not not_9 (not_9_out, or_5_out);
  and and_11 (and_11_out, not_9_out, and_3_out);
  J_K_Flip_Flop #(.trigger("falling")) j_k_ff_1 (
    .J(and_11_out), .K(1'b0), .clk(clock_2_out), .Qn(j_k_ff_1_qn), .reset(or_6_out));  // open: Q, preset
  or or_6 (or_6_out, and_12_out, or_1_out);
  and and_12 (and_12_out, clock_2_out, not_10_out, j_k_ff_2_qn);
  not not_10 (not_10_out, and_11_out);
  Clock clock_2 (.out(clock_2_out));
  and and_13 (and_13_out, j_k_ff_1_qn, j_k_ff_2_qn);
  Register PREVIEW_REGISTER (.D({rom_1_data_2, rom_1_data}), .en(1'b1), .clk(and_13_out), .clr(or_1_out));  // open: Q
  SN76489_Mockup sn76489_mockup_1 (
    .CLK(clock_2_out), .WE(and_13_out), .CE(and_13_out), .Data({rom_1_data_2, rom_1_data}),
    .Ready(sn76489_mockup_1_ready));
  not not_11 (not_11_out, sn76489_mockup_1_ready);
  J_K_Flip_Flop #(.trigger("falling")) j_k_ff_2 (
    .J(1'b1), .K(1'b0), .clk(not_11_out), .Qn(j_k_ff_2_qn), .reset(or_7_out));  // open: Q, preset
  or or_7 (or_7_out, or_1_out, not_12_out);
  not not_12 (not_12_out, j_k_ff_1_qn);

  // Notes on the sheet:
  //   contents of rom_1 (hex, n*v repeats v):
  //   e c a0 a1 a2 a3 a4 a5 a6 a7 a8 a9 aa ab 0 2 ac 2 82 ad 2 2 ae 2 41
  //   This "preview register" only exists to show the value sent to the SN76489.
  //   It is not a real part of the circuit, it's just for visualising in logisim.
endmodule

module SN76489_Mockup (
  input  CLK,
  input  WE,
  input  CE,
  input  [7:0] Data,
  output Ready
);

  wire and_1_out, counter_1_carry, not_1_out;

  not not_1 (not_1_out, CE);
  and and_1 (and_1_out, counter_1_carry, not_1_out);
  Counter #(.max('h1f), .ongoal("stay"), .width(5)) counter_1 (
    .clr(and_1_out), .count(WE), .clk(CLK), .carry(counter_1_carry));  // open: load, up, D, Q
  xnor xnor_1 (Ready, CE, counter_1_carry);
endmodule
